# Fritzing sketch 6502_computer (saved by Fritzing 0.9.3b)
breadboards: 6

parts:
  IC1 = 74HC08 Logic AND Gate [part_number=74HC08 package="DIP (Dual Inline) [THT]"]
  IC2 = IC, DIP package, 20 pins [chip_label=74HCT688E]
  IC3 = IC, DIP package, 20 pins [chip_label=74HCT688E]
  IC4 = IC, DIP package, 20 pins [chip_label=74HCT688E]
  IC5 = 74HC08 Logic AND Gate [part_number=74HC08 package="DIP (Dual Inline) [THT]"]
  Q1 = NPN-Transistor [package="TO92 [THT]"]
  IC6 = IC, DIP package, 16 pins [chip_label=74LS161A]
  Q2 = NPN-Transistor [package="TO92 [THT]"]
  U3 = 74HC595 [package="DIP16 [THT]"]
  U4 = 74HC595 [package="DIP16 [THT]"]
  IC7 = IC, DIP package, 20 pins [chip_label=74LS244AN]
  U5 = SWITCH_SPDT [package=kps-1290]
  IC8 = IC, DIP package, 40 pins [chip_label="WDC 65C02"]
  U6 = SWITCH_SPDT [package=kps-1290]
  IC9 = IC, DIP package, 14 pins [chip_label=74HC04]
  IC10 = IC, DIP package, 14 pins [chip_label=74HC04]
  IC11 = Voltage Regulator [package=to220-igo]
  XTAL1 = Crystal [frequency="1 MHz" package=THT]
  IC12 = 74HC08 Logic AND Gate [part_number=74HC08 package="DIP (Dual Inline) [THT]"]
  IC13 = IC, DIP package, 14 pins [chip_label=74HC04]
  S1 = Pushbutton [package="[THT]"]
  IC15 = IC, DIP package, 14 pins [chip_label=74HC04]
  IC16 = IC, DIP package, 28 pins [chip_label="CY7C199-35PC SRAM"]
  IC17 = IC, DIP package, 14 pins [chip_label=74LS32]
  IC18 = IC, DIP package, 14 pins [chip_label=74LS32]
  IC19 = IC, DIP package, 14 pins [chip_label=74LS32]
  IC20 = IC, DIP package, 14 pins [chip_label=74LS32]
  U8 = SWITCH_SPDT [package=kps-1290]
  U9 = 74HC595 [package="DIP16 [THT]"]
  U10 = 74HC595 [package="DIP16 [THT]"]
  U11 = 74HC595 [package="DIP16 [THT]"]
  U12 = SWITCH_SPDT [package=kps-1290]
  U13 = SWITCH_SPDT [package=kps-1290]
  U14 = SWITCH_SPDT [package=kps-1290]
  U15 = SWITCH_SPDT [package=kps-1290]
  U16 = SWITCH_SPDT [package=kps-1290]
  U17 = SWITCH_SPDT [package=kps-1290]
  U18 = SWITCH_SPDT [package=kps-1290]
  U19 = SWITCH_SPDT [package=kps-1290]
  U20 = SWITCH_SPDT [package=kps-1290]
  U21 = SWITCH_SPDT [package=kps-1290]
  IC21 = IC, DIP package, 14 pins [chip_label=74HC04]
  U22 = POT [package=3362u]
  LCD1 = LCD screen
  U23 = mini DIN 6 Connector [package=mini-din6]
  C2 = Ceramic Capacitor [capacitance=0.1µF package="200 mil [THT, multilayer]"]
  C3 = Ceramic Capacitor [capacitance=0.1µF package="200 mil [THT, multilayer]"]
  C4 = Ceramic Capacitor [capacitance=0.1µF package="200 mil [THT, multilayer]"]
  C5 = Ceramic Capacitor [capacitance=0.1µF package="200 mil [THT, multilayer]"]
  C6 = Ceramic Capacitor [capacitance=0.1µF package="200 mil [THT, multilayer]"]
  C7 = Electrolytic Capacitor [capacitance=220µF package="100 mil [THT, electrolytic]"]
  C8 = Electrolytic Capacitor [capacitance=220µF package="100 mil [THT, electrolytic]"]
  R1 = Resistor [tolerance=±5% resistance=10k package="2512 [SMD]"]
  R2 = Resistor [tolerance=±5% resistance=5k package="2512 [SMD]"]
  R3 = Resistor [tolerance=±5% resistance=10k package="2512 [SMD]"]
  R4 = Resistor [tolerance=±5% resistance=3.3k package="2512 [SMD]"]
  R5 = Resistor [tolerance=±5% resistance=5k package="2512 [SMD]"]
  C9 = Electrolytic Capacitor [capacitance=220µF package="100 mil [THT, electrolytic]"]
  C10 = Electrolytic Capacitor [capacitance=220µF package="100 mil [THT, electrolytic]"]
  C11 = Electrolytic Capacitor [capacitance=47µF package="100 mil [THT, electrolytic]"]
  C12 = Ceramic Capacitor [capacitance=0.1µF package="200 mil [THT, multilayer]"]
  C13 = Ceramic Capacitor [capacitance=0.1µF package="200 mil [THT, multilayer]"]
  C14 = Electrolytic Capacitor [capacitance=22µF package="100 mil [THT, electrolytic]"]
  C15 = Electrolytic Capacitor [capacitance=22µF package="100 mil [THT, electrolytic]"]
  C16 = Ceramic Capacitor [capacitance=0.01µF package="200 mil [THT, multilayer]"]
  R6 = Resistor [tolerance=±5% resistance=3.3k package="2512 [SMD]"]
  R7 = Resistor [tolerance=±5% resistance=3.3k package="2512 [SMD]"]
  R8 = Resistor [tolerance=±5% resistance=3.3k package="2512 [SMD]"]
  C17 = Ceramic Capacitor [capacitance=0.1µF package="200 mil [THT, multilayer]"]
  C18 = Ceramic Capacitor [capacitance=0.1µF package="200 mil [THT, multilayer]"]
  R9 = Resistor [tolerance=±5% resistance=3.3k package="2512 [SMD]"]
  C19 = Electrolytic Capacitor [capacitance=220µF package="100 mil [THT, electrolytic]"]
  C20 = Electrolytic Capacitor [capacitance=220µF package="100 mil [THT, electrolytic]"]
  IC14 = IC, DIP package, 28 pins [chip_label="28C256-15 EEPROM"]
  C21 = Electrolytic Capacitor [capacitance=220µF package="100 mil [THT, electrolytic]"]
  C22 = Ceramic Capacitor [capacitance=0.1µF package="200 mil [THT, multilayer]"]
  C23 = Ceramic Capacitor [capacitance=0.1µF package="200 mil [THT, multilayer]"]
  C24 = Electrolytic Capacitor [capacitance=220µF package="100 mil [THT, electrolytic]"]
  C25 = Electrolytic Capacitor [capacitance=220µF package="100 mil [THT, electrolytic]"]

nets:
  N1: IC1.1A, IC9.pin2
  N2: IC1.1B, IC9.pin4
  N3: IC1.1Y, U3.ST_CP, U4.ST_CP, IC9.pin5, IC10.pin5
  N4: IC1.2A, IC2.pin17, IC8.pin25, IC13.pin13, IC18.pin9
  N5: IC1.2B, IC9.pin6
  N6: IC1.2Y, IC21.pin1
  GND: IC1.GND, IC2.pin1, IC2.pin10, IC3.pin1, IC3.pin5, IC3.pin7, IC3.pin10, IC4.pin1, IC4.pin9, IC4.pin10, IC5.GND, Q1.C, IC6.pin8, Q2.C, U3.GND, U3.OE, U4.GND, U4.OE, IC7.pin10, IC8.pin21, IC9.pin7, IC10.pin7, IC11.IN, XTAL1.pin_1, IC12.GND, IC13.pin7, S1.Pin_3, S1.Pin_4, IC15.pin7, IC16.pin14, IC17.pin7, IC18.pin7, IC19.pin7, IC20.pin7, U9.GND, U10.GND, U11.GND, U13.S, U19.S, U21.O, IC21.pin7, U22.A, LCD1.VSS, LCD1.R/W, LCD1.LED-, U23.2, C2.0, C3.1, C5.1, C6.1, C7.-, C8.-, C9.-, C10.-, C11.-, C12.0, C13.0, C14.+, C15.-, C16.1, C17.1, C18.0, C19.-, C20.-, C21.-, C22.1, C23.1, C24.-, C25.-
  N7: IC1.4Y, IC9.pin9
  N8: IC1.4A, IC9.pin10
  N9: IC1.4B, IC9.pin12
  VCC: IC1.VCC, IC2.pin3, IC2.pin5, IC2.pin7, IC2.pin9, IC2.pin12, IC2.pin14, IC2.pin16, IC2.pin18, IC2.pin20, IC3.pin3, IC3.pin9, IC3.pin12, IC3.pin14, IC3.pin16, IC3.pin18, IC3.pin20, IC4.pin3, IC4.pin5, IC4.pin7, IC4.pin12, IC4.pin14, IC4.pin16, IC4.pin18, IC4.pin20, IC5.VCC, IC6.pin7, IC6.pin9, IC6.pin10, IC6.pin16, U3.MR, U3.VCC, U4.MR, U4.VCC, IC7.pin20, U5.O, IC8.pin8, IC8.pin18, IC8.pin38, IC9.pin14, IC10.pin14, IC11.OUT, XTAL1.pin_0, IC12.VCC, IC13.pin14, IC15.pin14, IC16.pin24, IC16.pin28, IC17.pin14, IC18.pin2, IC18.pin14, IC19.pin14, IC20.pin14, U8.O, U9.Q1, U9.MR, U9.VCC, U10.MR, U10.VCC, U11.MR, U11.VCC, U14.S, U18.S, IC21.pin14, U22.E, LCD1.VDD, LCD1.LED+, U23.1, C2.1, C4.0, C5.0, C7.+, C8.+, R2.Pin_0, R4.Pin_0, R5.Pin_0, C9.+, C10.+, C11.+, C12.1, C13.1, C15.+, C16.0, R6.Pin_0, R7.Pin_1, R8.Pin_1, C17.0, C18.1, R9.Pin_0, C19.+, C20.+, IC14.pin24, IC14.pin28, C21.+, C22.0, C23.0, C24.+, C25.+
  N10: IC2.pin2, IC8.pin17, IC16.pin25, IC18.pin1, U9.Q0, IC14.pin25
  N11: IC2.pin6, IC8.pin19, IC16.pin21, IC18.pin4, U9.Q2, IC14.pin21
  N12: IC2.pin8, IC8.pin20, IC16.pin23, IC18.pin5, U9.Q3, IC14.pin23
  N13: IC2.pin11, IC8.pin22, IC16.pin2, IC18.pin13, U9.Q4, IC14.pin2
  N14: IC2.pin13, IC8.pin23, IC16.pin26, IC18.pin12, U9.Q5, IC14.pin26
  N15: IC2.pin15, IC8.pin24, IC16.pin1, IC18.pin10, U9.Q6, IC14.pin1
  N16: IC2.pin19, IC9.pin1, IC9.pin13
  N17: IC3.pin2, IC4.pin2, IC8.pin9, IC16.pin10, IC17.pin1, U10.Q0, IC14.pin10
  N18: IC3.pin4, IC4.pin4, IC8.pin10, IC16.pin9, IC17.pin2, U10.Q1, IC14.pin9
  N19: IC3.pin6, IC4.pin6, IC8.pin11, IC16.pin8, IC17.pin4, U10.Q2, IC14.pin8
  N20: IC3.pin8, IC4.pin8, IC8.pin12, IC16.pin7, IC17.pin5, U10.Q3, IC14.pin7
  N21: IC3.pin11, IC4.pin11, IC8.pin13, IC16.pin6, IC17.pin13, U10.Q4, IC14.pin6
  N22: IC3.pin13, IC4.pin13, IC8.pin14, IC16.pin5, IC17.pin12, U10.Q5, IC14.pin5
  N23: IC3.pin15, IC4.pin15, IC8.pin15, IC16.pin4, IC17.pin10, U10.Q6, IC14.pin4
  N24: IC3.pin17, IC4.pin17, IC8.pin16, IC16.pin3, IC17.pin9, U10.Q7, IC14.pin3
  N25: IC3.pin19, IC9.pin11
  N26: IC4.pin19, IC9.pin3
  N27: IC5.3Y, R1.Pin_0, R3.Pin_1
  N28: IC5.3A, IC6.pin11
  N29: IC5.3B, IC5.4Y
  N30: IC5.4A, IC6.pin13
  N31: IC5.4B, IC6.pin14
  N32: Q1.E, IC10.pin3, U23.6, R2.Pin_1
  N33: Q1.B, R1.Pin_1
  N34: IC6.pin1, IC9.pin8
  N35: IC6.pin2, U3.SH_CP, U4.SH_CP, IC10.pin4
  N36: Q2.E, IC8.pin4, R4.Pin_1
  N37: Q2.B, R3.Pin_0
  N38: U3.Q2, IC7.pin11
  N39: U3.Q3, IC7.pin8
  N40: U3.Q4, IC7.pin13
  N41: U3.Q5, IC7.pin6
  N42: U3.Q6, IC7.pin16, IC8.pin31, IC16.pin13, U11.Q2, IC14.pin13
  N43: U3.Q7, IC7.pin4
  N44: U3.Q7', U4.DS
  N45: U3.DS, U23.5, R5.Pin_1
  N46: U4.Q1, IC7.pin2
  N47: U4.Q0, IC7.pin17
  N48: IC7.pin1, IC7.pin19, U5.P
  N49: IC7.pin3, IC8.pin32, IC16.pin12, U11.Q1, IC14.pin12
  N50: IC7.pin5, IC8.pin30, IC16.pin15, U11.Q3, LCD1.RS, IC14.pin15
  N51: IC7.pin7, IC8.pin28, IC16.pin17, U11.Q5, LCD1.DB5, IC14.pin17
  N52: IC7.pin9, IC8.pin26, IC16.pin19, U11.Q7, LCD1.DB7, IC14.pin19
  N53: IC7.pin12, IC8.pin27, IC16.pin18, U11.Q6, LCD1.DB6, IC14.pin18
  N54: IC7.pin14, IC8.pin29, IC16.pin16, U11.Q4, LCD1.DB4, IC14.pin16
  N55: IC7.pin18, IC8.pin33, IC16.pin11, U11.Q0, IC14.pin11
  N56: U5.S, IC10.pin6
  N57: IC8.pin2, R7.Pin_0
  N58: IC8.pin6, R8.Pin_0
  N59: IC8.pin34, IC15.pin1, IC15.pin11
  N60: IC8.pin36, U6.P
  N61: IC8.pin39, IC12.3B
  N62: IC8.pin40, S1.Pin_1, S1.Pin_2, R9.Pin_1
  N63: U6.S, R6.Pin_1
  N64: IC11.GND, C14.-
  N65: IC12.3Y, IC15.pin3
  N66: IC12.3A, IC15.pin2
  N67: IC12.4Y, IC13.pin11
  N68: IC12.4A, IC13.pin12
  N69: IC12.4B, IC20.pin11, IC21.pin13
  N70: IC13.pin10, U8.S
  N71: IC15.pin4, IC16.pin27
  N72: IC15.pin10, IC16.pin22
  N73: IC16.pin20, U8.P
  N74: IC17.pin3, IC19.pin5
  N75: IC17.pin6, IC19.pin4
  N76: IC17.pin8, IC19.pin9
  N77: IC17.pin11, IC19.pin10
  N78: IC18.pin3, IC19.pin1
  N79: IC18.pin6, IC19.pin2
  N80: IC18.pin8, IC19.pin12
  N81: IC18.pin11, IC19.pin13
  N82: IC19.pin3, IC20.pin4
  N83: IC19.pin6, IC20.pin5
  N84: IC19.pin8, IC20.pin9
  N85: IC19.pin11, IC20.pin10
  N86: IC20.pin6, IC20.pin13
  N87: IC20.pin8, IC20.pin12
  N88: U9.SH_CP, U10.SH_CP, U11.SH_CP, U16.P
  N89: U9.ST_CP, U10.ST_CP, U11.ST_CP, U12.P
  N90: U9.OE, U10.OE, U11.OE, U14.P
  N91: U9.DS, U13.P
  N92: U10.DS, U15.P
  N93: U11.DS, U17.P
  N94: U18.P, IC14.pin27
  N95: U19.P, IC14.pin22
  N96: U20.P, IC14.pin20
  N97: U20.S, IC21.pin2
  N98: IC21.pin12, LCD1.E
  N99: U22.S, LCD1.V0

notes:
  PS/2 Keyboard
  Data
  Clock
  To 9V DC
  To GND
  6
  4
  3
  5
  2
  12
  11
  10
  GND
  To microcontroller pin:
